// Logisim project ALU.circ as structural Verilog: 2 circuits, main circuit main
module main (
);

  wire alu_1_flag_0, button_1_out, button_2_out, button_3_out, button_4_out, button_5_out, t_ff_1_q,
       t_ff_2_q, t_ff_3_q, t_ff_4_q, t_ff_5_q;
  wire [7:0] controlled_buffer_1_out;

  Button button_1 (.out(button_1_out));
  Button button_2 (.out(button_2_out));
  Button button_3 (.out(button_3_out));
  T_Flip_Flop t_ff_1 (.clk(button_1_out), .T(button_1_out), .Q(t_ff_1_q));  // open: Qn, preset, reset, en
  T_Flip_Flop t_ff_2 (.clk(button_2_out), .T(button_2_out), .Q(t_ff_2_q));  // open: Qn, preset, reset, en
  T_Flip_Flop t_ff_3 (.clk(button_3_out), .T(button_3_out), .Q(t_ff_3_q));  // open: Qn, preset, reset, en
  Button button_4 (.out(button_4_out));
  Button button_5 (.out(button_5_out));
  T_Flip_Flop t_ff_4 (.clk(button_4_out), .T(button_4_out), .Q(t_ff_4_q));  // open: Qn, preset, reset, en
  T_Flip_Flop t_ff_5 (.clk(button_5_out), .T(button_5_out), .Q(t_ff_5_q));  // open: Qn, preset, reset, en
  assign controlled_buffer_1_out = t_ff_4_q ? 8'ha : 8'bz;  // Controlled_Buffer controlled_buffer_1
  assign controlled_buffer_1_out = t_ff_5_q ? 8'h81 : 8'bz;  // Controlled_Buffer controlled_buffer_2
  ALU alu_1 (
    .ALU1_WR(t_ff_1_q), .ALU2_WR(t_ff_2_q), .ALU_OE(t_ff_3_q), .ALU_DATA(controlled_buffer_1_out),
    .FLAG_0(alu_1_flag_0));
  DotMatrix #(.matrixcols(1), .matrixrows(8)) dotmatrix_1 (.col0(controlled_buffer_1_out));
  LED led_1 (.in(alu_1_flag_0));
endmodule

module ALU (
  input  [7:0] ALU_DATA,
  input  ALU1_WR,
  input  ALU2_WR,
  input  ALU_OE,
  output FLAG_0
);

  wire [7:0] adder_1_out, ALU1_q, ALU2_q;

  Register ALU1 (.D(ALU_DATA), .en(1'b1), .Q(ALU1_q), .clk(ALU1_WR));  // open: clr
  Register ALU2 (.D(ALU_DATA), .en(1'b1), .Q(ALU2_q), .clk(ALU2_WR));  // open: clr
  Adder adder_1 (.a(ALU1_q), .b(ALU2_q), .out(adder_1_out));  // open: cin, cout
  assign ALU_DATA = ALU_OE ? adder_1_out : 8'bz;  // Controlled_Buffer controlled_buffer_1
  Comparator comparator_1 (.a(adder_1_out), .b({8{1'b0}}), .eq(FLAG_0));  // open: gt, lt
endmodule
