// Logisim project PROJ.circ as structural Verilog: 9 circuits, main circuit main
module main (
);

  wire alu_1_flag_0, control_logic_1_alu1_wr, control_logic_1_alu2_wr, control_logic_1_alu_oe,
       control_logic_1_ir_wr, control_logic_1_mar_oe, control_logic_1_mar_wr,
       control_logic_1_pc_load_not_count, control_logic_1_pc_load_or_count, control_logic_1_pc_oe,
       control_logic_1_ram_load, control_logic_1_ram_store, control_logic_1_rom_oe, undriven;
  wire [7:0] control_logic_1_r_oe, control_logic_1_r_wr, instruction_register_1_ir_out,
       program_counter_1_pc_ab, registers_1_r_db_out;

  Clock clock_1 ();  // open: out
  CONTROL_LOGIC control_logic_1 (
    .INSTRUCTION(instruction_register_1_ir_out), .FLAG_0(alu_1_flag_0), .R_WR(control_logic_1_r_wr),
    .R_OE(control_logic_1_r_oe), .ALU1_WR(control_logic_1_alu1_wr), .ALU2_WR(control_logic_1_alu2_wr),
    .ALU_OE(control_logic_1_alu_oe), .IR_WR(control_logic_1_ir_wr), .PC_OE(control_logic_1_pc_oe),
    .PC_LOAD_NOT_COUNT(control_logic_1_pc_load_not_count),
    .PC_LOAD_OR_COUNT(control_logic_1_pc_load_or_count), .MAR_WR(control_logic_1_mar_wr),
    .MAR_OE(control_logic_1_mar_oe), .ROM_OE(control_logic_1_rom_oe), .RAM_STORE(control_logic_1_ram_store),
    .RAM_LOAD(control_logic_1_ram_load));
  DotMatrix #(.inputtype("row"), .matrixcols(8), .matrixrows(1)) dotmatrix_1 (.row0(program_counter_1_pc_ab));
  REGISTERS registers_1 (
    .RESET(undriven), .R_WR(control_logic_1_r_wr), .R_DB_IN(registers_1_r_db_out),
    .R_OE(control_logic_1_r_oe), .R_DB_OUT(registers_1_r_db_out));
  ALU alu_1 (
    .ALU_DB_IN(registers_1_r_db_out), .ALU1_WR(control_logic_1_alu1_wr), .ALU2_WR(control_logic_1_alu2_wr),
    .RESET(undriven), .ALU_OE(control_logic_1_alu_oe), .ALU_DB_OUT(registers_1_r_db_out),
    .FLAG_0(alu_1_flag_0));
  INSTRUCTION_REGISTER instruction_register_1 (
    .IR_WR(control_logic_1_ir_wr), .RESET(undriven), .IR_DB(registers_1_r_db_out),
    .IR_OUT(instruction_register_1_ir_out));
  PROGRAM_COUNTER program_counter_1 (
    .RESET(undriven), .LOAD_NOT_COUNT(control_logic_1_pc_load_not_count),
    .LOAD_OR_COUNT(control_logic_1_pc_load_or_count), .PC_DB(registers_1_r_db_out),
    .PC_OE(control_logic_1_pc_oe), .PC_AB(program_counter_1_pc_ab));
  MAR mar_1 (
    .MAR_DB(registers_1_r_db_out), .MAR_WR(control_logic_1_mar_wr), .RESET(undriven),
    .MAR_OE(control_logic_1_mar_oe), .MAR_AB(program_counter_1_pc_ab));
  ROM_1 rom_1_1 (.ROM_AB(program_counter_1_pc_ab), .ROM_OE(control_logic_1_rom_oe), .ROM_DB(registers_1_r_db_out));
  RAM_1 ram_1_1 (
    .RAM_OE(control_logic_1_ram_load), .RAM_BD_IN(registers_1_r_db_out), .RAM_WR(control_logic_1_ram_store),
    .RAM_AB(program_counter_1_pc_ab), .RAM_BD_OUT(registers_1_r_db_out));
  DotMatrix #(.inputtype("row"), .matrixcols(8), .matrixrows(1)) dotmatrix_2 (.row0(registers_1_r_db_out));
endmodule

module ALU (
  input  [7:0] ALU_DB_IN,
  input  ALU1_WR,
  input  ALU2_WR,
  input  ALU_OE,
  input  RESET,
  output [7:0] ALU_DB_OUT,
  output FLAG_0
);

  wire or_1_out;
  wire [7:0] adder_1_out, ALU1_q, ALU2_q, controlled_buffer_1_out;

  or or_1 (or_1_out, ALU2_WR, ALU1_WR);
  Register #(.trigger("falling")) ALU1 (.D(controlled_buffer_1_out), .en(1'b1), .clk(ALU1_WR), .Q(ALU1_q), .clr(RESET));
  Register #(.trigger("falling")) ALU2 (.D(controlled_buffer_1_out), .en(1'b1), .clk(ALU2_WR), .Q(ALU2_q), .clr(RESET));
  Adder adder_1 (.a(ALU1_q), .b(ALU2_q), .out(adder_1_out));  // open: cin, cout
  assign controlled_buffer_1_out = ALU_OE ? adder_1_out : 8'bz;  // Controlled_Buffer controlled_buffer_1
  assign controlled_buffer_1_out = or_1_out ? ALU_DB_IN : 8'bz;  // Controlled_Buffer controlled_buffer_2
  Comparator comparator_1 (.a(adder_1_out), .b({8{1'b0}}), .eq(FLAG_0));  // open: gt, lt
  assign ALU_DB_OUT = ALU_OE ? controlled_buffer_1_out : 8'bz;  // Controlled_Buffer controlled_buffer_3
endmodule

module REGISTERS (
  input  [7:0] R_WR,
  input  [7:0] R_DB_IN,
  input  [7:0] R_OE,
  input  RESET,
  output [7:0] R_DB_OUT
);

  wire or_1_out, or_2_out;
  wire [7:0] controlled_buffer_1_out, register_1_q, register_2_q, register_3_q, register_4_q, register_5_q,
       register_6_q, register_7_q, register_8_q;

  Register #(.trigger("falling")) register_1 (
    .D(controlled_buffer_1_out), .en(1'b1), .clk(R_WR[0]), .Q(register_1_q), .clr(RESET));
  Register #(.trigger("falling")) register_2 (
    .D(controlled_buffer_1_out), .en(1'b1), .clk(R_WR[1]), .Q(register_2_q), .clr(RESET));
  Register #(.trigger("falling")) register_3 (
    .D(controlled_buffer_1_out), .en(1'b1), .clk(R_WR[2]), .Q(register_3_q), .clr(RESET));
  Register #(.trigger("falling")) register_4 (
    .D(controlled_buffer_1_out), .en(1'b1), .clk(R_WR[3]), .Q(register_4_q), .clr(RESET));
  Register #(.trigger("falling")) register_5 (
    .D(controlled_buffer_1_out), .en(1'b1), .clk(R_WR[4]), .Q(register_5_q), .clr(RESET));
  Register #(.trigger("falling")) register_6 (
    .D(controlled_buffer_1_out), .en(1'b1), .clk(R_WR[5]), .Q(register_6_q), .clr(RESET));
  Register #(.trigger("falling")) register_7 (
    .D(controlled_buffer_1_out), .en(1'b1), .clk(R_WR[6]), .Q(register_7_q), .clr(RESET));
  Register #(.trigger("falling")) register_8 (
    .D(controlled_buffer_1_out), .en(1'b1), .clk(R_WR[7]), .Q(register_8_q), .clr(RESET));
  or or_1 (or_1_out, R_WR[0], R_WR[1], R_WR[2], R_WR[3], R_WR[4], R_WR[5], R_WR[6], R_WR[7]);
  assign controlled_buffer_1_out = R_OE[0] ? register_1_q : 8'bz;  // Controlled_Buffer controlled_buffer_1
  assign controlled_buffer_1_out = R_OE[1] ? register_2_q : 8'bz;  // Controlled_Buffer controlled_buffer_2
  assign controlled_buffer_1_out = R_OE[2] ? register_3_q : 8'bz;  // Controlled_Buffer controlled_buffer_3
  assign controlled_buffer_1_out = R_OE[3] ? register_4_q : 8'bz;  // Controlled_Buffer controlled_buffer_4
  assign controlled_buffer_1_out = R_OE[4] ? register_5_q : 8'bz;  // Controlled_Buffer controlled_buffer_5
  assign controlled_buffer_1_out = R_OE[5] ? register_6_q : 8'bz;  // Controlled_Buffer controlled_buffer_6
  assign controlled_buffer_1_out = R_OE[6] ? register_7_q : 8'bz;  // Controlled_Buffer controlled_buffer_7
  assign controlled_buffer_1_out = R_OE[7] ? register_8_q : 8'bz;  // Controlled_Buffer controlled_buffer_8
  assign controlled_buffer_1_out = or_1_out ? R_DB_IN : 8'bz;  // Controlled_Buffer controlled_buffer_9
  assign R_DB_OUT = or_2_out ? controlled_buffer_1_out : 8'bz;  // Controlled_Buffer controlled_buffer_10
  or or_2 (or_2_out, R_OE[7], R_OE[6], R_OE[5], R_OE[4], R_OE[3], R_OE[2], R_OE[1], R_OE[0]);
endmodule

module ROM_1 (
  input  [7:0] ROM_AB,
  input  ROM_OE,
  output [7:0] ROM_DB
);

  wire [7:0] rom_1_data;

  Clock clock_1 ();  // open: out
  ROM rom_1 (.addr(ROM_AB), .data(rom_1_data));
  assign ROM_DB = ROM_OE ? rom_1_data : 8'bz;  // Controlled_Buffer controlled_buffer_1

  // Notes on the sheet:
  //   contents of rom_1 (hex, n*v repeats v):
  //   10 1 14 6 9 29 39 4e 58 14 ff 24 54
endmodule

module INSTRUCTION_REGISTER (
  input  [7:0] IR_DB,
  input  IR_WR,
  input  RESET,
  output [7:0] IR_OUT
);

  wire [7:0] controlled_buffer_1_out;

  assign controlled_buffer_1_out = IR_WR ? IR_DB : 8'bz;  // Controlled_Buffer controlled_buffer_1
  Register #(.trigger("falling")) register_1 (
    .D(controlled_buffer_1_out), .en(1'b1), .clk(IR_WR), .Q(IR_OUT), .clr(RESET));
endmodule

module PROGRAM_COUNTER (
  input  LOAD_NOT_COUNT,
  input  LOAD_OR_COUNT,
  input  [7:0] PC_DB,
  input  PC_OE,
  input  RESET,
  output [7:0] PC_AB
);

  wire [7:0] counter_1_q;

  Counter counter_1 (
    .clr(RESET), .load(LOAD_NOT_COUNT), .up(1'b1), .count(1'b1), .clk(LOAD_OR_COUNT), .D(PC_DB),
    .Q(counter_1_q));  // open: carry
  assign PC_AB = PC_OE ? counter_1_q : 8'bz;  // Controlled_Buffer controlled_buffer_1
endmodule

module CONTROL_LOGIC (
  input  [7:0] INSTRUCTION,
  input  FLAG_0,
  output [7:0] R_WR,
  output [7:0] R_OE,
  output ALU1_WR,
  output ALU2_WR,
  output ALU_OE,
  output IR_WR,
  output PC_OE,
  output PC_LOAD_NOT_COUNT,
  output PC_LOAD_OR_COUNT,
  output MAR_WR,
  output MAR_OE,
  output ROM_OE,
  output RAM_STORE,
  output RAM_LOAD
);

  wire and_1_out, clock_1_out, comparator_1_eq, comparator_2_eq, not_1_out, not_2_out, not_3_out, or_1_out,
       undriven;
  wire [3:0] demultiplexer_1_out0, demultiplexer_2_out0;
  wire [7:0] controlled_buffer_1_out, controlled_buffer_3_out, counter_1_q, register_1_q, rom_1_data;
  wire [15:0] rom_2_data;

  Demultiplexer #(.select(2)) demultiplexer_1 (
    .out0(demultiplexer_1_out0[0]), .out1(demultiplexer_1_out0[1]), .out2(demultiplexer_1_out0[2]),
    .out3(demultiplexer_1_out0[3]), .in(1'b1), .sel(INSTRUCTION[1:0]));
  ROM #(.addrWidth(4)) rom_1 (.addr(INSTRUCTION[7:4]), .data(rom_1_data));
  Demultiplexer #(.select(2)) demultiplexer_2 (
    .out0(demultiplexer_2_out0[0]), .out1(demultiplexer_2_out0[1]), .out2(demultiplexer_2_out0[2]),
    .out3(demultiplexer_2_out0[3]), .in(1'b1), .sel(INSTRUCTION[3:2]));
  Counter counter_1 (
    .clr(rom_2_data[0]), .load(and_1_out), .up(1'b1), .count(1'b1), .clk(clock_1_out), .D(rom_1_data),
    .Q(counter_1_q));  // open: carry
  Register #(.trigger("falling")) register_1 (
    .D(counter_1_q), .en(1'b1), .clk(clock_1_out), .Q(register_1_q), .clr(undriven));
  Comparator #(.mode("unsigned"), .width(4)) comparator_1 (
    .a(INSTRUCTION[7:4]), .b(4'b0101), .eq(comparator_1_eq));  // open: gt, lt
  Comparator comparator_2 (.a(8'h9), .b(counter_1_q), .eq(comparator_2_eq));  // open: gt, lt
  not not_1 (not_1_out, comparator_1_eq);
  ROM #(.dataWidth(16)) rom_2 (
    .addr(register_1_q),
    .data({rom_2_data[15:13], ALU1_WR, ALU2_WR, ALU_OE, IR_WR, PC_OE, PC_LOAD_NOT_COUNT, PC_LOAD_OR_COUNT, MAR_WR, MAR_OE, ROM_OE, RAM_STORE, RAM_LOAD, rom_2_data[0]}));
  or or_1 (or_1_out, not_1_out, FLAG_0);
  and and_1 (and_1_out, or_1_out, comparator_2_eq);
  Clock clock_1 (.out(clock_1_out));
  not not_2 (not_2_out, rom_2_data[15]);
  assign controlled_buffer_1_out = rom_2_data[15] ? {4'b0000, demultiplexer_1_out0} : 8'bz;  // Controlled_Buffer controlled_buffer_1
  assign controlled_buffer_1_out = not_2_out ? {4'b0000, demultiplexer_2_out0} : 8'bz;  // Controlled_Buffer controlled_buffer_2
  assign controlled_buffer_3_out = not_3_out ? {4'b0000, demultiplexer_1_out0} : 8'bz;  // Controlled_Buffer controlled_buffer_3
  assign controlled_buffer_3_out = rom_2_data[15] ? {4'b0000, demultiplexer_2_out0} : 8'bz;  // Controlled_Buffer controlled_buffer_4
  not not_3 (not_3_out, rom_2_data[15]);
  assign R_WR = rom_2_data[14] ? controlled_buffer_1_out : 8'bz;  // Controlled_Buffer controlled_buffer_5
  assign R_OE = rom_2_data[13] ? controlled_buffer_3_out : 8'bz;  // Controlled_Buffer controlled_buffer_6

  // Notes on the sheet:
  //   contents of rom_1 (hex, n*v repeats v):
  //   b 10 19 27 34 3f
  //   contents of rom_2 (hex, n*v repeats v):
  //   0 100 108 308 108 100 0 40 0 0 1 2000 6000 2000 0 1 100 108 4108 108 100 0 40 0 1 8000 a000 b000
  //   8000 0 2000 2800 2000 0 400 4400 400 0 1 8000 a000 a020 a000 8000 0 10 2010 2014 2010 10 0 1 2000
  //   2020 2000 0 10 12 4012 12 10 0 1 8000 a000 a080 a0c0 a080 a000 8000 0 1
endmodule

module RAM_1 (
  input  [7:0] RAM_AB,
  input  RAM_OE,
  input  [7:0] RAM_BD_IN,
  input  RAM_WR,
  output [7:0] RAM_BD_OUT
);

  wire [7:0] controlled_buffer_2_out, ram_1_dout;

  assign RAM_BD_OUT = RAM_OE ? ram_1_dout : 8'bz;  // Controlled_Buffer controlled_buffer_1
  assign controlled_buffer_2_out = RAM_WR ? RAM_BD_IN : 8'bz;  // Controlled_Buffer controlled_buffer_2
  RAM #(.trigger("high")) ram_1 (
    .addr(RAM_AB), .we(RAM_WR), .oe(RAM_OE), .din(controlled_buffer_2_out), .dout(ram_1_dout));
endmodule

module MAR (
  input  [7:0] MAR_DB,
  input  MAR_WR,
  input  MAR_OE,
  input  RESET,
  output [7:0] MAR_AB
);

  wire [7:0] controlled_buffer_1_out, register_1_q;

  Register #(.trigger("falling")) register_1 (
    .D(controlled_buffer_1_out), .en(1'b1), .clk(MAR_WR), .Q(register_1_q), .clr(RESET));
  assign controlled_buffer_1_out = MAR_WR ? MAR_DB : 8'bz;  // Controlled_Buffer controlled_buffer_1
  assign MAR_AB = MAR_OE ? register_1_q : 8'bz;  // Controlled_Buffer controlled_buffer_2
endmodule
